// Logisim project D8421+2.circ as structural Verilog: 1 circuit, main circuit main
// 10unsigned
module main (
  input  [3:0] D8421,
  output [3:0] D8421_2
);

  wire and_1_out, and_2_out, and_3_out, and_4_out, and_5_out, and_6_out, and_7_out, and_8_out, not_1_out,
       not_2_out, not_3_out, not_4_out, not_5_out, not_6_out, not_7_out, not_8_out, not_9_out, not_10_out,
       not_11_out, not_12_out, not_13_out;

  // Probe on D8421
  not not_1 (not_1_out, D8421[3]);
  not not_2 (not_2_out, D8421[3]);
  not not_3 (not_3_out, D8421[2]);
  not not_4 (not_4_out, D8421[1]);
  not not_5 (not_5_out, D8421[2]);
  not not_6 (not_6_out, D8421[1]);
  not not_7 (not_7_out, D8421[3]);
  not not_8 (not_8_out, D8421[1]);
  not not_9 (not_9_out, D8421[2]);
  not not_10 (not_10_out, D8421[1]);
  not not_11 (not_11_out, D8421[3]);
  not not_12 (not_12_out, D8421[2]);
  not not_13 (not_13_out, D8421[1]);
  and and_1 (and_1_out, not_2_out, D8421[2], D8421[1]);
  and and_2 (and_2_out, D8421[3], not_3_out, not_4_out);
  and and_3 (and_3_out, not_1_out, not_5_out, D8421[1]);
  and and_4 (and_4_out, not_1_out, D8421[2], not_6_out);
  and and_5 (and_5_out, not_7_out, not_8_out);
  and and_6 (and_6_out, not_9_out, not_10_out);
  and and_7 (and_7_out, not_11_out, D8421[0]);
  and and_8 (and_8_out, not_12_out, not_13_out, D8421[0]);
  or or_1 (D8421_2[3], and_1_out, and_2_out);
  or or_2 (D8421_2[2], and_3_out, and_4_out);
  or or_3 (D8421_2[1], and_5_out, and_6_out);
  or or_4 (D8421_2[0], and_7_out, and_8_out);
  // Probe on D8421_2
endmodule
