// Logisim project VICHITATEL.circ as structural Verilog: 2 circuits, main circuit main
module main (
  input  S,
  output [2:0] out_2
);

  wire and_1_out, and_2_out, clock_1_out, not_1_out, not_2_out;

  Clock clock_1 (.out(clock_1_out));
  T_Flip_Flop O3 (.clk(S), .T(clock_1_out), .Q(out_2[0]));  // open: Qn, preset, reset, en
  not not_1 (not_1_out, out_2[0]);
  T_Flip_Flop O2 (.clk(S), .T(and_1_out), .Q(out_2[1]));  // open: Qn, preset, reset, en
  not not_2 (not_2_out, out_2[1]);
  and and_1 (and_1_out, not_1_out, clock_1_out);
  T_Flip_Flop O1 (.clk(S), .T(and_2_out), .Q(out_2[2]));  // open: Qn, preset, reset, en
  and and_2 (and_2_out, not_2_out, not_1_out, clock_1_out);
endmodule

module JK (
  output out_1,
  output out_2,
  output out_3
);

  J_K_Flip_Flop j_k_ff_1 (.J(out_1), .K(out_3), .Q(out_2));  // open: clk, Qn, preset, en, reset
endmodule
